# Fritzing sketch 1Wire Unterverteiler USB-C (saved by Fritzing 1.0.1rc)
stripboards: 1

parts:
  Bauteil1 = Adafruit USB Type C Breakout MRA
  Bauteil2 = Adafruit USB Type C Breakout MRA
  Bauteil3 = Adafruit USB Type C Breakout MRA

nets:
  N1: Bauteil1.VBUS, Bauteil2.VBUS, Bauteil3.VBUS
  N2: Bauteil1.GND, Bauteil2.D-
  N3: Bauteil1.CC1, Bauteil3.CC1
  N4: Bauteil1.D-, Bauteil3.D-
  N5: Bauteil1.D+, Bauteil2.CC1
  N6: Bauteil1.CC2, Bauteil2.CC2, Bauteil3.CC2
  GND: Bauteil2.GND, Bauteil3.GND
  N7: Bauteil2.D+, Bauteil3.D+

notes:
  12V +
  1W Dat <=
  1W GND =>
  1W Dat =>
  1W GND <=
  5V +
  1
  2
  3

custom parts:
  Adafruit USB Type C Breakout MRA: breakout board for USB Type C socket 6 Pin
