# Fritzing sketch 1WireTemp (saved by Fritzing 1.0.1rc)
breadboards: 1

parts:
  TFT1 = 1.44" SPI TFT Graphics Display 128x128 - MR 8pin [package=THT]
  Sensor1 = TTP223B Capacitive Touch Sensor Module
  M1 = Arduino NANO RP2040 CONNECT with headers

nets:
  GND: TFT1.pin1, Sensor1.GND, M1.VIN
  N1: TFT1.pin2, M1.GND-4, M1.GND-29
  N2: TFT1.pin3, M1.D7
  N3: TFT1.pin4, M1.D6
  N4: TFT1.pin5, M1.D5
  N5: TFT1.pin6, M1.D11
  N6: TFT1.pin7, M1.D13
  N7: TFT1.pin8, M1.D3
  N8: Sensor1.SIG, M1.D18
  N9: M1.D27, M1.RESET-28

custom parts:
  TTP223B Capacitive Touch Sensor Module: The TTP223B capacitive touch sensor module uses the TTP223B IC. The appropriate voltage is approximately 2 to 5.5 volts.
