# Fritzing sketch DS2438 Sondenadapter (saved by Fritzing 1.0.1rc)
stripboards: 1

parts:
  VR2 = DS2438 [part_number=DS2438 package=SO]
  J5 = Camdenboss CTB0158-3 [part_number=CTB0158-3 package=THT]
  J3 = screw terminal, 4 pins

nets:
  N1: VR2.pin_1, J5.pin3, J3.pin2
  N2: VR2.pin_4, VR2.pin_5, J5.pin2, J3.pin4
  N3: VR2.pin_8, J3.pin1
  N4: J5.pin1, J3.pin3

notes:
  1W
  GND
  +12V
  +5V
  0-2V

custom parts:
  DS2438: 1-Wire DS2438 Smart Battery Monitor
